# Fritzing sketch gas (saved by Fritzing 0.9.3b)
breadboards: 1

parts:
  U1 = GAS_SENSOR [part_number=Air_quality package=mq-3]
  U2 = GAS_SENSOR [part_number=CO package=mq-3]
  U3 = GAS_SENSOR [part_number=CO2 package=mq-3]
  Part1 = Arduino Yun  # not connected

nets:
  N1: U1.H1, U2.H1, U3.H1
  N2: U1.H2, U2.H2, U3.H2
